# Fritzing sketch 7SEG_PressureSensor_FullColorLED (saved by Fritzing 0.8.5b)
breadboards: 1

parts:
  パーツ1 = Arduino Uno (Rev3)
  LED1 = 7-SEGMENT-4DIGIT-YOUNGSUN [package=7-segment-4digit-youngsun-longpads]
  R1 = Resistor [tolerance=±5% resistance=220 package=THT]
  R2 = Resistor [tolerance=±5% resistance=220 package=THT]
  R3 = Resistor [tolerance=±5% resistance=220 package=THT]
  S1 = Pushbutton [package="[THT]"]
  R4 = Resistor [tolerance=±5% resistance=220 package=THT]
  LED2 = RGB LED (com. anode, rbg) [package="5 mm [THT]"]
  R5 = Resistor [tolerance=±5% resistance=220 package=THT]
  R6 = Resistor [tolerance=±5% resistance=220 package=THT]
  R7 = Resistor [tolerance=±5% resistance=220 package=THT]
  J1 = Basic Force Sensing Resistor (FSR) [package=THT]
  R8 = Resistor [tolerance=±5% resistance=220 package=THT]

nets:
  N1: パーツ1.A0, パーツ1.5V, S1.Pin_3, S1.Pin_4, R8.Pin_0
  N2: パーツ1.A1, S1.Pin_1, S1.Pin_2, R4.Pin_0
  N3: パーツ1.D8, R2.Pin_1
  N4: パーツ1.D9_PWM, LED1.APOS-A
  N5: パーツ1.D10_PWM/SS, LED1.B, R3.Pin_0
  N6: パーツ1.D11_PWM/MOSI, LED1.C
  N7: パーツ1.D12/MISO, LED1.A
  N8: パーツ1.D13/SCK, R5.Pin_0, R6.Pin_0, R7.Pin_0
  N9: パーツ1.GND, R4.Pin_1, J1.pin_0
  N10: パーツ1.D2, LED1.DIG2
  N11: パーツ1.D3_PWM, LED1.D
  N12: パーツ1.D4, LED1.COL-A
  N13: パーツ1.D5_PWM, LED1.E
  N14: パーツ1.D6_PWM, LED1.DIG3
  N15: パーツ1.D7, R1.Pin_1
  N16: LED1.DP, R1.Pin_0
  N17: LED1.F, R2.Pin_0
  N18: LED1.COL-C, R3.Pin_1
  N19: LED2.red_cathode, R5.Pin_1
  N20: LED2.common_anode, R6.Pin_1
  N21: LED2.green_cathode, R7.Pin_1
  N22: J1.pin_1, R8.Pin_1
