# Fritzing sketch Untitled Sketch (saved by Fritzing 0.8.5b)
breadboards: 1

parts:
  パーツ1 = Arduino Uno (Rev3)
  LED1 = RGB LED (com. anode, rbg) [package="5 mm [THT]"]
  R1 = Resistor [tolerance=±5% resistance=220 package=THT]
  R2 = Resistor [tolerance=±5% resistance=220 package=THT]
  R3 = Resistor [tolerance=±5% resistance=220 package=THT]
  S1 = Pushbutton [package="[THT]"]
  S2 = Pushbutton [package="[THT]"]
  S3 = Pushbutton [package="[THT]"]
  S4 = Pushbutton [package="[THT]"]
  R4 = Resistor [tolerance=±5% resistance=220 package=THT]
  R5 = Resistor [tolerance=±5% resistance=220 package=THT]
  R6 = Resistor [tolerance=±5% resistance=220 package=THT]
  R7 = Resistor [tolerance=±5% resistance=220 package=THT]

nets:
  N1: パーツ1.D8, パーツ1.D9_PWM, パーツ1.D6_PWM, パーツ1.D7, S1.Pin_3, S1.Pin_4, S2.Pin_3, S2.Pin_4, S3.Pin_3, S3.Pin_4, S4.Pin_3, S4.Pin_4, R4.Pin_0, R5.Pin_0, R6.Pin_0, R7.Pin_0
  N2: パーツ1.D10_PWM/SS, R3.Pin_1
  N3: パーツ1.D11_PWM/MOSI, R2.Pin_1
  N4: パーツ1.D12/MISO, R1.Pin_1
  N5: パーツ1.GND, R4.Pin_1, R5.Pin_1, R6.Pin_1, R7.Pin_1
  N6: LED1.red_cathode, R3.Pin_0
  N7: LED1.common_anode, R2.Pin_0
  N8: LED1.green_cathode, R1.Pin_0
  N9: S1.Pin_1, S1.Pin_2
  N10: S2.Pin_1, S2.Pin_2
  N11: S3.Pin_1, S3.Pin_2
  N12: S4.Pin_1, S4.Pin_2
