# Fritzing sketch Untitled Sketch (saved by Fritzing 0.8.5b)
breadboards: 4
stripboards: 1

parts:
  パーツ1 = Arduino Uno (Rev3)
  U1 = 74HC595 [package="DIP16 [THT]"]
  U2 = 74HC595 [package="DIP16 [THT]"]
  R1 = Resistor [tolerance=±5% resistance=220 package=THT]
  LED1 = LED - 5mm [color="Red (633nm)" package="5 mm [THT]"]
  LED2 = LED - 5mm [color="Red (633nm)" package="5 mm [THT]"]
  LED3 = LED - 5mm [color="Red (633nm)" package="5 mm [THT]"]
  LED4 = LED - 5mm [color="Red (633nm)" package="5 mm [THT]"]
  LED5 = LED - 5mm [color="Red (633nm)" package="5 mm [THT]"]
  LED6 = LED - 5mm [color="Red (633nm)" package="5 mm [THT]"]
  LED7 = LED - 5mm [color="Red (633nm)" package="5 mm [THT]"]
  LED8 = LED - 5mm [color="Red (633nm)" package="5 mm [THT]"]
  LED9 = LED - 5mm [color="Red (633nm)" package="5 mm [THT]"]
  LED10 = LED - 5mm [color="Red (633nm)" package="5 mm [THT]"]
  LED11 = LED - 5mm [color="Red (633nm)" package="5 mm [THT]"]
  LED12 = LED - 5mm [color="Red (633nm)" package="5 mm [THT]"]
  LED13 = LED - 5mm [color="Red (633nm)" package="5 mm [THT]"]
  LED14 = LED - 5mm [color="Red (633nm)" package="5 mm [THT]"]
  LED15 = LED - 5mm [color="Red (633nm)" package="5 mm [THT]"]
  LED16 = LED - 5mm [color="Red (633nm)" package="5 mm [THT]"]
  U3 = 74HC595 [package="DIP16 [THT]"]
  U4 = 74HC595 [package="DIP16 [THT]"]
  R2 = Resistor [tolerance=±5% resistance=220 package=THT]
  R3 = Resistor [tolerance=±5% resistance=220 package=THT]
  R4 = Resistor [tolerance=±5% resistance=220 package=THT]  # not connected
  R5 = Resistor [tolerance=±5% resistance=220 package=THT]
  R6 = Resistor [tolerance=±5% resistance=220 package=THT]
  R7 = Resistor [tolerance=±5% resistance=220 package=THT]
  R8 = Resistor [tolerance=±5% resistance=220 package=THT]
  R9 = Resistor [tolerance=±5% resistance=220 package=THT]
  R10 = Resistor [tolerance=±5% resistance=220 package=THT]
  R11 = Resistor [tolerance=±5% resistance=220 package=THT]

nets:
  N1: パーツ1.D8, U1.ST_CP, U2.ST_CP, R1.Pin_0
  N2: パーツ1.D11_PWM/MOSI, U1.DS
  N3: パーツ1.D12/MISO, U1.SH_CP, U2.SH_CP
  N4: パーツ1.D2, U3.ST_CP, U4.ST_CP, R2.Pin_0
  N5: パーツ1.D5_PWM, U3.DS
  N6: パーツ1.D6_PWM, U3.SH_CP, U4.SH_CP
  VCC: パーツ1.5V, U1.MR, U1.VCC, U2.MR, U2.VCC, LED1.anode, U3.MR, U3.VCC, U4.MR, U4.VCC
  GND: パーツ1.GND, U1.GND, U1.OE, U2.GND, U2.OE, R1.Pin_1, LED1.cathode, LED2.cathode, LED3.cathode, LED4.cathode, LED5.cathode, LED6.cathode, LED7.cathode, LED8.cathode, LED9.cathode, LED10.cathode, LED11.cathode, LED12.cathode, LED13.cathode, LED14.cathode, LED15.cathode, LED16.cathode, U3.GND, U3.OE, U4.GND, U4.OE, R2.Pin_1
  N7: U1.Q1, LED2.anode
  N8: U1.Q2, LED3.anode
  N9: U1.Q3, LED4.anode
  N10: U1.Q4, LED5.anode
  N11: U1.Q5, LED6.anode
  N12: U1.Q6, LED7.anode
  N13: U1.Q7, LED8.anode
  N14: U1.Q7', U2.DS
  N15: U2.Q1, LED10.anode
  N16: U2.Q2, LED11.anode
  N17: U2.Q3, LED12.anode
  N18: U2.Q4, LED13.anode
  N19: U2.Q5, LED14.anode
  N20: U2.Q6, LED15.anode
  N21: U2.Q7, LED16.anode
  N22: U2.Q0, LED9.anode
  N23: U3.Q7, R3.Pin_0, R5.Pin_0
  N24: U3.Q7', U4.DS
  N25: U4.Q1, R10.Pin_1
  N26: U4.Q2, R9.Pin_1
  N27: U4.Q3, R8.Pin_1
  N28: U4.Q4, R7.Pin_1
  N29: U4.Q5, R6.Pin_1
  N30: U4.Q6, R5.Pin_1
  N31: U4.Q7, R3.Pin_1
  N32: U4.Q0, R11.Pin_1
