# Fritzing sketch Untitled Sketch (saved by Fritzing 0.8.5b)
breadboards: 2

parts:
  パーツ1 = Arduino Uno (Rev3)
  U1 = 74HC595 [package="DIP16 [THT]"]
  U2 = 74HC595 [package="DIP16 [THT]"]
  R1 = Resistor [tolerance=±5% resistance=220 package=THT]
  LED1 = LED - 5mm [color="Red (633nm)" package="5 mm [THT]"]
  LED2 = LED - 5mm [color="Red (633nm)" package="5 mm [THT]"]
  LED3 = LED - 5mm [color="Red (633nm)" package="5 mm [THT]"]
  LED4 = LED - 5mm [color="Red (633nm)" package="5 mm [THT]"]
  LED5 = LED - 5mm [color="Red (633nm)" package="5 mm [THT]"]
  LED6 = LED - 5mm [color="Red (633nm)" package="5 mm [THT]"]
  LED7 = LED - 5mm [color="Red (633nm)" package="5 mm [THT]"]
  LED8 = LED - 5mm [color="Red (633nm)" package="5 mm [THT]"]
  LED9 = LED - 5mm [color="Red (633nm)" package="5 mm [THT]"]
  LED10 = LED - 5mm [color="Red (633nm)" package="5 mm [THT]"]
  LED11 = LED - 5mm [color="Red (633nm)" package="5 mm [THT]"]
  LED12 = LED - 5mm [color="Red (633nm)" package="5 mm [THT]"]
  LED13 = LED - 5mm [color="Red (633nm)" package="5 mm [THT]"]
  LED14 = LED - 5mm [color="Red (633nm)" package="5 mm [THT]"]
  LED15 = LED - 5mm [color="Red (633nm)" package="5 mm [THT]"]
  LED16 = LED - 5mm [color="Red (633nm)" package="5 mm [THT]"]

nets:
  N1: パーツ1.D8, U1.ST_CP, U2.ST_CP, R1.Pin_0
  N2: パーツ1.D11_PWM/MOSI, U1.DS
  N3: パーツ1.D12/MISO, U1.SH_CP, U2.SH_CP
  VCC: パーツ1.5V, U1.MR, U1.VCC, U2.MR, U2.VCC, LED1.anode
  GND: パーツ1.GND, U1.GND, U1.OE, U2.GND, U2.OE, R1.Pin_1, LED1.cathode, LED2.cathode, LED3.cathode, LED4.cathode, LED5.cathode, LED6.cathode, LED7.cathode, LED8.cathode, LED9.cathode, LED10.cathode, LED11.cathode, LED12.cathode, LED13.cathode, LED14.cathode, LED15.cathode, LED16.cathode
  N4: U1.Q1, LED2.anode
  N5: U1.Q2, LED3.anode
  N6: U1.Q3, LED4.anode
  N7: U1.Q4, LED5.anode
  N8: U1.Q5, LED6.anode
  N9: U1.Q6, LED7.anode
  N10: U1.Q7, LED8.anode
  N11: U1.Q7', U2.DS
  N12: U2.Q1, LED10.anode
  N13: U2.Q2, LED11.anode
  N14: U2.Q3, LED12.anode
  N15: U2.Q4, LED13.anode
  N16: U2.Q5, LED14.anode
  N17: U2.Q6, LED15.anode
  N18: U2.Q7, LED16.anode
  N19: U2.Q0, LED9.anode
